// Logisim project minha-ula.circ as structural Verilog: 25 circuits, main circuit mux2
module mux2 (
  input  I0,
  input  I1,
  input  Sel,
  output out_4
);

  wire and_1_out, and_2_out;

  and and_1 (and_1_out, I0, ~Sel);  // AND_Gate
  and and_2 (and_2_out, I1, Sel);
  or or_1 (out_4, and_1_out, and_2_out);
endmodule

module mux2_4bits (
  input  [3:0] I0,
  input  [3:0] I1,
  input  in_3,
  output [3:0] out_4
);

  wire [3:0] and_1_out, and_2_out;

  assign and_1_out = I0 & ~{4{in_3}};  // AND_Gate and_1, 4 bits wide
  assign and_2_out = I1 & {4{in_3}};  // AND_Gate and_2, 4 bits wide
  assign out_4 = and_1_out | and_2_out;  // OR_Gate or_1, 4 bits wide
endmodule

module mux4 (
  input  l0,
  input  l1,
  input  l2,
  input  l3,
  input  sel1,
  input  sel0,
  output out_7
);

  wire mux2_1_out_4, mux2_2_out_4;

  mux2 mux2_1 (.I0(l0), .I1(l1), .Sel(sel0), .out_4(mux2_1_out_4));
  mux2 mux2_2 (.I0(l2), .I1(l3), .Sel(sel0), .out_4(mux2_2_out_4));
  mux2 mux2_3 (.I0(mux2_1_out_4), .I1(mux2_2_out_4), .Sel(sel1), .out_4(out_7));
endmodule

module mux4b (
  input  l0,
  input  l1,
  input  l2,
  input  l3,
  input  [1:0] in_5,
  output out_6
);

  wire mux2_1_out_4, mux2_2_out_4;

  mux2 mux2_1 (.I0(l0), .I1(l1), .Sel(in_5[0]), .out_4(mux2_1_out_4));
  mux2 mux2_2 (.I0(l2), .I1(l3), .Sel(in_5[0]), .out_4(mux2_2_out_4));
  mux2 mux2_3 (.I0(mux2_1_out_4), .I1(mux2_2_out_4), .Sel(in_5[1]), .out_4(out_6));
endmodule

module mux8 (
  input  l0,
  input  l1,
  input  l2,
  input  l3,
  input  l4,
  input  l5,
  input  l6,
  input  l7,
  input  sel2,
  input  sel1,
  input  sel0,
  output out_12
);

  wire mux4_1_out_7, mux4_2_out_7;

  mux4 mux4_1 (.l0(l0), .l1(l1), .l2(l2), .l3(l3), .sel1(sel1), .sel0(sel0), .out_7(mux4_1_out_7));
  mux4 mux4_2 (.l0(l4), .l1(l5), .l2(l6), .l3(l7), .sel1(sel1), .sel0(sel0), .out_7(mux4_2_out_7));
  mux2 mux2_1 (.I0(mux4_1_out_7), .I1(mux4_2_out_7), .Sel(sel2), .out_4(out_12));
endmodule

module mux8b (
  input  l0,
  input  l1,
  input  l2,
  input  l3,
  input  l4,
  input  l5,
  input  l6,
  input  l7,
  input  [2:0] sel,
  output out_10
);

  wire mux4_1_out_7, mux4_2_out_7;

  mux4 mux4_1 (.l0(l0), .l1(l1), .l2(l2), .l3(l3), .sel1(sel[1]), .sel0(sel[0]), .out_7(mux4_1_out_7));
  mux4 mux4_2 (.l0(l4), .l1(l5), .l2(l6), .l3(l7), .sel1(sel[1]), .sel0(sel[0]), .out_7(mux4_2_out_7));
  mux2 mux2_1 (.I0(mux4_1_out_7), .I1(mux4_2_out_7), .Sel(sel[2]), .out_4(out_10));
endmodule

module mux16 (
  input  l0,
  input  l1,
  input  l2,
  input  l3,
  input  l4,
  input  l5,
  input  l6,
  input  l7,
  input  l8,
  input  l9,
  input  l10,
  input  l11,
  input  l12,
  input  l13,
  input  l14,
  input  l15,
  input  sel3,
  input  sel2,
  input  sel1,
  input  sel0,
  output out_21
);

  wire mux8_1_out_12, mux8_2_out_12;

  mux8 mux8_1 (
    .l0(l0), .l1(l1), .l2(l2), .l3(l3), .l4(l4), .l5(l5), .l6(l6), .l7(l7), .sel2(sel2), .sel1(sel1),
    .sel0(sel0), .out_12(mux8_1_out_12));
  mux8 mux8_2 (
    .l0(l8), .l1(l9), .l2(l10), .l3(l11), .l4(l12), .l5(l13), .l6(l14), .l7(l15), .sel2(sel2), .sel1(sel1),
    .sel0(sel0), .out_12(mux8_2_out_12));
  mux2 mux2_1 (.I0(mux8_1_out_12), .I1(mux8_2_out_12), .Sel(sel3), .out_4(out_21));
endmodule

module mux16b (
  input  l0,
  input  l1,
  input  l2,
  input  l3,
  input  l4,
  input  l5,
  input  l6,
  input  l7,
  input  l8,
  input  l9,
  input  l10,
  input  l11,
  input  l12,
  input  l13,
  input  l14,
  input  l15,
  input  [3:0] in_17,
  output out_18
);

  wire mux8_1_out_12, mux8_2_out_12;

  mux8 mux8_1 (
    .l0(l0), .l1(l1), .l2(l2), .l3(l3), .l4(l4), .l5(l5), .l6(l6), .l7(l7), .sel2(in_17[2]), .sel1(in_17[1]),
    .sel0(in_17[0]), .out_12(mux8_1_out_12));
  mux8 mux8_2 (
    .l0(l8), .l1(l9), .l2(l10), .l3(l11), .l4(l12), .l5(l13), .l6(l14), .l7(l15), .sel2(in_17[2]),
    .sel1(in_17[1]), .sel0(in_17[0]), .out_12(mux8_2_out_12));
  mux2 mux2_1 (.I0(mux8_1_out_12), .I1(mux8_2_out_12), .Sel(in_17[3]), .out_4(out_18));
endmodule

module mux32 (
  input  l0,
  input  l1,
  input  l2,
  input  l3,
  input  l4,
  input  l5,
  input  l6,
  input  l7,
  input  l8,
  input  l9,
  input  l10,
  input  l11,
  input  l12,
  input  l13,
  input  l14,
  input  l15,
  input  l16,
  input  l17,
  input  l18,
  input  l19,
  input  l20,
  input  l21,
  input  l22,
  input  l23,
  input  l24,
  input  l25,
  input  l26,
  input  l27,
  input  l28,
  input  l29,
  input  l30,
  input  sel5,
  input  sel3,
  input  sel2,
  input  sel1,
  input  sel0,
  input  l31,
  output out_38
);

  wire mux16_1_out_21, mux16_2_out_21;

  mux16 mux16_1 (
    .l0(l0), .l1(l1), .l2(l2), .l3(l3), .l4(l4), .l5(l5), .l6(l6), .l7(l7), .l8(l8), .l9(l9), .l10(l10),
    .l11(l11), .l12(l12), .l13(l13), .l14(l14), .l15(l15), .sel3(sel3), .sel2(sel2), .sel1(sel1),
    .sel0(sel0), .out_21(mux16_1_out_21));
  mux16 mux16_2 (
    .l0(l16), .l1(l17), .l2(l18), .l3(l19), .l4(l20), .l5(l21), .l6(l22), .l7(l23), .l8(l24), .l9(l25),
    .l10(l26), .l11(l27), .l12(l28), .l13(l29), .l14(l30), .l15(l31), .sel3(sel3), .sel2(sel2), .sel1(sel1),
    .sel0(sel0), .out_21(mux16_2_out_21));
  mux2 mux2_1 (.I0(mux16_1_out_21), .I1(mux16_2_out_21), .Sel(sel5), .out_4(out_38));
endmodule

module mux32b (
  input  l0,
  input  l1,
  input  l2,
  input  l3,
  input  l4,
  input  l5,
  input  l6,
  input  l7,
  input  l8,
  input  l9,
  input  l10,
  input  l11,
  input  l12,
  input  l13,
  input  l14,
  input  l15,
  input  l16,
  input  l17,
  input  l18,
  input  l19,
  input  l20,
  input  l21,
  input  l22,
  input  l23,
  input  l24,
  input  l25,
  input  l26,
  input  l27,
  input  l28,
  input  l29,
  input  l30,
  input  l31,
  input  [4:0] in_33,
  output out_34
);

  wire mux16_1_out_21, mux16_2_out_21;

  mux16 mux16_1 (
    .l0(l0), .l1(l1), .l2(l2), .l3(l3), .l4(l4), .l5(l5), .l6(l6), .l7(l7), .l8(l8), .l9(l9), .l10(l10),
    .l11(l11), .l12(l12), .l13(l13), .l14(l14), .l15(l15), .sel3(in_33[3]), .sel2(in_33[2]), .sel1(in_33[1]),
    .sel0(in_33[0]), .out_21(mux16_1_out_21));
  mux16 mux16_2 (
    .l0(l16), .l1(l17), .l2(l18), .l3(l19), .l4(l20), .l5(l21), .l6(l22), .l7(l23), .l8(l24), .l9(l25),
    .l10(l26), .l11(l27), .l12(l28), .l13(l29), .l14(l30), .l15(l31), .sel3(in_33[3]), .sel2(in_33[2]),
    .sel1(in_33[1]), .sel0(in_33[0]), .out_21(mux16_2_out_21));
  mux2 mux2_1 (.I0(mux16_1_out_21), .I1(mux16_2_out_21), .Sel(in_33[4]), .out_4(out_34));
endmodule

module somador (
  input  vem1,
  input  B,
  input  A,
  output soma,
  output vai1
);

  wire and_1_out, and_2_out, and_3_out, and_4_out, or_1_out, xnor_1_out, xor_1_out;

  xor xor_1 (xor_1_out, B, A);
  or or_1 (or_1_out, B, A);
  xnor xnor_1 (xnor_1_out, B, A);
  and and_1 (and_1_out, B, A);
  and and_2 (and_2_out, or_1_out, vem1);
  and and_3 (and_3_out, xnor_1_out, vem1);
  and and_4 (and_4_out, xor_1_out, ~vem1);  // AND_Gate
  or or_2 (vai1, and_1_out, and_2_out);
  or or_3 (soma, and_3_out, and_4_out);
endmodule

module ShiftLeftLogical (
  input  [3:0] in_1,
  input  shift,
  output [3:0] out_3
);

  mux2_4bits mux2_4bits_1 (.I0(in_1), .I1({in_1[2:0], 1'b0}), .in_3(shift), .out_4(out_3));

  // Notes on the sheet:
  //   Deslocar para esquerda é o mesmo que multiplicar por 2
endmodule

module ShiftRightLogical (
  input  [3:0] in_1,
  input  in_2,
  output [3:0] out_3
);

  mux2_4bits mux2_4bits_1 (.I0(in_1), .I1({1'b0, in_1[3:1]}), .in_3(in_2), .out_4(out_3));

  // Notes on the sheet:
  //   Deslocar para direita é o mesmo que dividir por 2
endmodule

module ShiftLeftArith (
  input  [3:0] in_1,
  input  in_2,
  output [3:0] out_3
);

  mux2_4bits mux2_4bits_1 (.I0(in_1), .I1({in_1[2:0], in_1[0]}), .in_3(in_2), .out_4(out_3));
endmodule

module ShiftRightArith (
  input  [3:0] in_1,
  input  in_2,
  output [3:0] out_3
);

  mux2_4bits mux2_4bits_1 (.I0(in_1), .I1({{2{in_1[3]}}, in_1[2:1]}), .in_3(in_2), .out_4(out_3));
endmodule

module UlaCell (
  input  a,
  input  b,
  input  vem1,
  input  [4:0] OpCode,
  output saida,
  output vai1
);

  wire and_1_out, or_1_out, somador_1_soma, xor_1_out;

  and and_1 (and_1_out, b, a);
  or or_1 (or_1_out, b, a);
  somador somador_1 (.B(b), .A(a), .vem1(vem1), .vai1(vai1), .soma(somador_1_soma));
  xor xor_1 (xor_1_out, b, a);
  mux32b mux32b_1 (
    .l0(and_1_out), .l1(or_1_out), .l2(somador_1_soma), .l3(xor_1_out), .l4(a), .l5(b), .l6(a), .l7(b),
    .l8(a), .l9(b), .in_33(OpCode), .out_34(saida));  // open: l10, l11, l12, l13, l14, l15, l16, l17, l18, l19, l20, l21, l22, l23, l24, l25, l26, l27, l28, l29, l30, l31
endmodule

module SLLDetector (
  input  [4:0] UlaOpCode,
  output saida
);

  and and_1 (saida, ~UlaOpCode[4], ~UlaOpCode[3], UlaOpCode[2], ~UlaOpCode[1], UlaOpCode[0]);  // AND_Gate
endmodule

module SLLADetector (
  input  [4:0] UlaOpCode,
  output out_2
);

  and and_1 (out_2, ~UlaOpCode[0], ~UlaOpCode[1], UlaOpCode[2], ~UlaOpCode[3], ~UlaOpCode[4]);  // AND_Gate
endmodule

module SRLADetector (
  input  [4:0] UlaOpCode,
  output out_2
);

  and and_1 (out_2, ~UlaOpCode[0], UlaOpCode[1], UlaOpCode[2], ~UlaOpCode[3], ~UlaOpCode[4]);  // AND_Gate
endmodule

module SRLBDetector (
  input  [4:0] UlaOpCode,
  output out_2
);

  and and_1 (out_2, ~UlaOpCode[4], ~UlaOpCode[3], UlaOpCode[2], UlaOpCode[1], UlaOpCode[0]);  // AND_Gate
endmodule

module SLAADetector (
  input  [4:0] UlaOpCode,
  output out_2
);

  and and_1 (out_2, ~UlaOpCode[4], UlaOpCode[3], ~UlaOpCode[2], ~UlaOpCode[1], ~UlaOpCode[0]);  // AND_Gate
endmodule

module SLBDetector (
  input  [4:0] UlaOpCode,
  output out_2
);

  and and_1 (out_2, ~UlaOpCode[4], UlaOpCode[3], ~UlaOpCode[2], ~UlaOpCode[1], UlaOpCode[0]);  // AND_Gate
endmodule

module ULA (
  input  [3:0] A,
  input  [3:0] B,
  input  [4:0] UlaOpCode,
  output [3:0] out_4
);

  wire slladetector_1_out_2, slldetector_1_saida, ulacell_2_vai1, ulacell_3_vai1, ulacell_4_vai1;
  wire [3:0] SLLA_out_3, SLLB_out_3;

  ShiftLeftLogical SLLA (.in_1(A), .shift(slladetector_1_out_2), .out_3(SLLA_out_3));
  SLLADetector slladetector_1 (.out_2(slladetector_1_out_2), .UlaOpCode(UlaOpCode));
  ShiftLeftLogical SLLB (.in_1(B), .shift(slldetector_1_saida), .out_3(SLLB_out_3));
  SLLDetector slldetector_1 (.saida(slldetector_1_saida), .UlaOpCode(UlaOpCode));
  UlaCell ulacell_1 (
    .a(SLLA_out_3[3]), .b(SLLB_out_3[3]), .OpCode(UlaOpCode), .saida(out_4[3]), .vem1(ulacell_2_vai1));  // open: vai1
  UlaCell ulacell_2 (
    .vai1(ulacell_2_vai1), .a(SLLA_out_3[2]), .b(SLLB_out_3[2]), .OpCode(UlaOpCode), .saida(out_4[2]),
    .vem1(ulacell_3_vai1));
  UlaCell ulacell_3 (
    .vai1(ulacell_3_vai1), .a(SLLA_out_3[1]), .b(SLLB_out_3[1]), .OpCode(UlaOpCode), .saida(out_4[1]),
    .vem1(ulacell_4_vai1));
  UlaCell ulacell_4 (
    .vai1(ulacell_4_vai1), .a(SLLA_out_3[0]), .b(SLLB_out_3[0]), .OpCode(UlaOpCode), .saida(out_4[0]),
    .vem1(1'b0));

  // Notes on the sheet:
  //   00000 - AND
  //   00001 - OR
  //   00010 - SOMADOR
  //   00011 - XOR
  //   00100 - SLL A
  //   00101 - SLL B
  //   00110 - SRL A
  //   00111 - SRL B
endmodule

module ULATest (
  input  [3:0] A,
  input  [3:0] B,
  input  [4:0] UlaOpCode,
  output [3:0] out_4
);

  wire slladetector_1_out_2, slldetector_1_saida, srladetector_1_out_2, srlbdetector_1_out_2, ulacell_2_vai1,
       ulacell_3_vai1, ulacell_4_vai1;
  wire [3:0] mux2_4bits_1_out_4, mux2_4bits_2_out_4, SLLA_out_3, SLLB_out_3, SRLA_out_3, SRLB_out_3;

  ShiftLeftLogical SLLA (.in_1(A), .shift(slladetector_1_out_2), .out_3(SLLA_out_3));
  SLLADetector slladetector_1 (.out_2(slladetector_1_out_2), .UlaOpCode(UlaOpCode));
  ShiftLeftLogical SLLB (.in_1(B), .shift(slldetector_1_saida), .out_3(SLLB_out_3));
  SLLDetector slldetector_1 (.saida(slldetector_1_saida), .UlaOpCode(UlaOpCode));
  SRLADetector srladetector_1 (.out_2(srladetector_1_out_2), .UlaOpCode(UlaOpCode));
  ShiftRightLogical SRLA (.in_1(A), .in_2(srladetector_1_out_2), .out_3(SRLA_out_3));
  ShiftRightLogical SRLB (.in_1(B), .in_2(srlbdetector_1_out_2), .out_3(SRLB_out_3));
  SRLBDetector srlbdetector_1 (.out_2(srlbdetector_1_out_2), .UlaOpCode(UlaOpCode));
  mux2_4bits mux2_4bits_1 (.I0(SLLA_out_3), .I1(SRLA_out_3), .in_3(srladetector_1_out_2), .out_4(mux2_4bits_1_out_4));
  mux2_4bits mux2_4bits_2 (.I0(SLLB_out_3), .I1(SRLB_out_3), .in_3(srlbdetector_1_out_2), .out_4(mux2_4bits_2_out_4));
  UlaCell ulacell_1 (
    .a(mux2_4bits_1_out_4[3]), .b(mux2_4bits_2_out_4[3]), .OpCode(UlaOpCode), .saida(out_4[3]),
    .vem1(ulacell_2_vai1));  // open: vai1
  UlaCell ulacell_2 (
    .vai1(ulacell_2_vai1), .a(mux2_4bits_1_out_4[2]), .b(mux2_4bits_2_out_4[2]), .OpCode(UlaOpCode),
    .saida(out_4[2]), .vem1(ulacell_3_vai1));
  UlaCell ulacell_3 (
    .vai1(ulacell_3_vai1), .a(mux2_4bits_1_out_4[1]), .b(mux2_4bits_2_out_4[1]), .OpCode(UlaOpCode),
    .saida(out_4[1]), .vem1(ulacell_4_vai1));
  UlaCell ulacell_4 (
    .vai1(ulacell_4_vai1), .a(mux2_4bits_1_out_4[0]), .b(mux2_4bits_2_out_4[0]), .OpCode(UlaOpCode),
    .saida(out_4[0]), .vem1(1'b0));

  // Notes on the sheet:
  //   00000 - AND
  //   00001 - OR
  //   00010 - SOMADOR
  //   00011 - XOR
  //   00100 - SLL A
  //   00101 - SLL B
  //   00110 - SRL A
  //   00111 - SRL B
  //   FALTAM FAZER:
  //   01000 - SLA A
  //   01001 - SLA B
endmodule

module ULA32bits (
  input  [31:0] B,
  input  [31:0] A,
  input  [4:0] ULAOpCode,
  output [31:0] result
);

  wire ulacell_1_vai1, ulacell_3_vai1, ulacell_4_vai1, ulacell_5_vai1, ulacell_6_vai1, ulacell_7_vai1,
       ulacell_8_vai1, ulacell_9_vai1, ulacell_10_vai1, ulacell_11_vai1, ulacell_12_vai1, ulacell_13_vai1,
       ulacell_14_vai1, ulacell_15_vai1, ulacell_16_vai1, ulacell_17_vai1, ulacell_18_vai1, ulacell_19_vai1,
       ulacell_20_vai1, ulacell_21_vai1, ulacell_22_vai1, ulacell_23_vai1, ulacell_24_vai1, ulacell_25_vai1,
       ulacell_26_vai1, ulacell_27_vai1, ulacell_28_vai1, ulacell_29_vai1, ulacell_30_vai1, ulacell_31_vai1,
       ulacell_32_vai1;

  UlaCell ulacell_1 (
    .vai1(ulacell_1_vai1), .a(A[30]), .b(B[30]), .OpCode(ULAOpCode), .saida(result[30]), .vem1(ulacell_3_vai1));
  UlaCell ulacell_2 (
    .a(A[31]), .b(B[31]), .OpCode(ULAOpCode), .saida(result[31]), .vem1(ulacell_1_vai1));  // open: vai1
  UlaCell ulacell_3 (
    .vai1(ulacell_3_vai1), .a(A[29]), .b(B[29]), .OpCode(ULAOpCode), .saida(result[29]), .vem1(ulacell_5_vai1));
  UlaCell ulacell_4 (
    .vai1(ulacell_4_vai1), .a(A[27]), .b(B[27]), .OpCode(ULAOpCode), .saida(result[27]), .vem1(ulacell_6_vai1));
  UlaCell ulacell_5 (
    .vai1(ulacell_5_vai1), .a(A[28]), .b(B[28]), .OpCode(ULAOpCode), .saida(result[28]), .vem1(ulacell_4_vai1));
  UlaCell ulacell_6 (
    .vai1(ulacell_6_vai1), .a(A[26]), .b(B[26]), .OpCode(ULAOpCode), .saida(result[26]), .vem1(ulacell_7_vai1));
  UlaCell ulacell_7 (
    .vai1(ulacell_7_vai1), .a(A[25]), .b(B[25]), .OpCode(ULAOpCode), .saida(result[25]), .vem1(ulacell_8_vai1));
  UlaCell ulacell_8 (
    .vai1(ulacell_8_vai1), .a(A[24]), .b(B[24]), .OpCode(ULAOpCode), .saida(result[24]),
    .vem1(ulacell_10_vai1));
  UlaCell ulacell_9 (
    .vai1(ulacell_9_vai1), .a(A[22]), .b(B[22]), .OpCode(ULAOpCode), .saida(result[22]),
    .vem1(ulacell_11_vai1));
  UlaCell ulacell_10 (
    .vai1(ulacell_10_vai1), .a(A[23]), .b(B[23]), .OpCode(ULAOpCode), .saida(result[23]),
    .vem1(ulacell_9_vai1));
  UlaCell ulacell_11 (
    .vai1(ulacell_11_vai1), .a(A[21]), .b(B[21]), .OpCode(ULAOpCode), .saida(result[21]),
    .vem1(ulacell_13_vai1));
  UlaCell ulacell_12 (
    .vai1(ulacell_12_vai1), .a(A[19]), .b(B[19]), .OpCode(ULAOpCode), .saida(result[19]),
    .vem1(ulacell_15_vai1));
  UlaCell ulacell_13 (
    .vai1(ulacell_13_vai1), .a(A[20]), .b(B[20]), .OpCode(ULAOpCode), .saida(result[20]),
    .vem1(ulacell_12_vai1));
  UlaCell ulacell_14 (
    .vai1(ulacell_14_vai1), .a(A[17]), .b(B[17]), .OpCode(ULAOpCode), .saida(result[17]),
    .vem1(ulacell_16_vai1));
  UlaCell ulacell_15 (
    .vai1(ulacell_15_vai1), .a(A[18]), .b(B[18]), .OpCode(ULAOpCode), .saida(result[18]),
    .vem1(ulacell_14_vai1));
  UlaCell ulacell_16 (
    .vai1(ulacell_16_vai1), .a(A[16]), .b(B[16]), .OpCode(ULAOpCode), .saida(result[16]),
    .vem1(ulacell_17_vai1));
  UlaCell ulacell_17 (
    .vai1(ulacell_17_vai1), .a(A[15]), .b(B[15]), .OpCode(ULAOpCode), .saida(result[15]),
    .vem1(ulacell_18_vai1));
  UlaCell ulacell_18 (
    .vai1(ulacell_18_vai1), .a(A[14]), .b(B[14]), .OpCode(ULAOpCode), .saida(result[14]),
    .vem1(ulacell_19_vai1));
  UlaCell ulacell_19 (
    .vai1(ulacell_19_vai1), .a(A[13]), .b(B[13]), .OpCode(ULAOpCode), .saida(result[13]),
    .vem1(ulacell_20_vai1));
  UlaCell ulacell_20 (
    .vai1(ulacell_20_vai1), .a(A[12]), .b(B[12]), .OpCode(ULAOpCode), .saida(result[12]),
    .vem1(ulacell_21_vai1));
  UlaCell ulacell_21 (
    .vai1(ulacell_21_vai1), .a(A[11]), .b(B[11]), .OpCode(ULAOpCode), .saida(result[11]),
    .vem1(ulacell_22_vai1));
  UlaCell ulacell_22 (
    .vai1(ulacell_22_vai1), .a(A[10]), .b(B[10]), .OpCode(ULAOpCode), .saida(result[10]),
    .vem1(ulacell_23_vai1));
  UlaCell ulacell_23 (
    .vai1(ulacell_23_vai1), .a(A[9]), .b(B[9]), .OpCode(ULAOpCode), .saida(result[9]), .vem1(ulacell_24_vai1));
  UlaCell ulacell_24 (
    .vai1(ulacell_24_vai1), .a(A[8]), .b(B[8]), .OpCode(ULAOpCode), .saida(result[8]), .vem1(ulacell_25_vai1));
  UlaCell ulacell_25 (
    .vai1(ulacell_25_vai1), .a(A[7]), .b(B[7]), .OpCode(ULAOpCode), .saida(result[7]), .vem1(ulacell_26_vai1));
  UlaCell ulacell_26 (
    .vai1(ulacell_26_vai1), .a(A[6]), .b(B[6]), .OpCode(ULAOpCode), .saida(result[6]), .vem1(ulacell_27_vai1));
  UlaCell ulacell_27 (
    .vai1(ulacell_27_vai1), .a(A[5]), .b(B[5]), .OpCode(ULAOpCode), .saida(result[5]), .vem1(ulacell_28_vai1));
  UlaCell ulacell_28 (
    .vai1(ulacell_28_vai1), .a(A[4]), .b(B[4]), .OpCode(ULAOpCode), .saida(result[4]), .vem1(ulacell_29_vai1));
  UlaCell ulacell_29 (
    .vai1(ulacell_29_vai1), .a(A[3]), .b(B[3]), .OpCode(ULAOpCode), .saida(result[3]), .vem1(ulacell_30_vai1));
  UlaCell ulacell_30 (
    .vai1(ulacell_30_vai1), .a(A[2]), .b(B[2]), .OpCode(ULAOpCode), .saida(result[2]), .vem1(ulacell_31_vai1));
  UlaCell ulacell_31 (
    .vai1(ulacell_31_vai1), .a(A[1]), .b(B[1]), .OpCode(ULAOpCode), .saida(result[1]), .vem1(ulacell_32_vai1));
  UlaCell ulacell_32 (.vai1(ulacell_32_vai1), .a(A[0]), .b(B[0]), .OpCode(ULAOpCode), .saida(result[0]), .vem1(1'b0));

  // Notes on the sheet:
  //   00001 - OR
  //   00000 - AND
  //   00010 - SOMADOR
  //   00011 - XOR
  //   00100 - SLL A
  //   00101 - SLL B
  //   00110 - SRL A
  //   00111 - SRL B
  //   FALTAM FAZER:
  //   01000 - SLA A
  //   01001 - SLA B
endmodule
